# Fritzing sketch WizardBot (saved by Fritzing 0.9.3b)
breadboards: 1

parts:
  U1 = L298 [package=multiwatt15_6400bgheatsink]
  Part1 = Arduino Uno (Rev3)
  VCC1 = Battery block 9V
  M1 = DC Motor
  M2 = DC Motor

nets:
  N1: U1.OUT1, M1.pin_1
  N2: U1.OUT2, M1.pin_2
  N3: U1.VS, Part1.VIN, VCC1.+
  N4: U1.IN1, Part1.D6_PWM
  N5: U1.ENA, Part1.D9_PWM
  N6: U1.IN2, Part1.D5_PWM
  GND: U1.GND, Part1.GND, VCC1.-
  N7: U1.IN3, Part1.D4
  N8: U1.ENB, Part1.D10_PWM/SS
  N9: U1.IN4, Part1.D3_PWM
  N10: U1.OUT3, M2.pin_1
  N11: U1.OUT4, M2.pin_2
